# Fritzing sketch hook-to-nodemcuV3-serial-adapter-and-buttons (saved by Fritzing 0.9.6b)

parts:
  U1 = NodeMCU V3.0
  ESP-12N = ESP8266-12 [part_number=ESP8266-12]
  R1 = Resistor [tolerance=±5% resistance=220 package="0805 [SMD]"]
  R2 = Resistor [tolerance=±5% resistance=220 package="0805 [SMD]"]

nets:
  N1: U1.D3, ESP-12N.GPIO0
  3V3: U1.3V3, ESP-12N.VCC, R1.Pin_1
  GND: U1.GND, U1.EN, ESP-12N.GND, R2.Pin_1
  N2: U1.RX, ESP-12N.RXD
  N3: U1.TX, ESP-12N.TXD
  N4: U1.RST, ESP-12N.REST
  N5: ESP-12N.CH_PD, R1.Pin_0
  N6: ESP-12N.GPIO15, R2.Pin_0

custom parts:
  NodeMCU V3.0: ESP8266 based NodeMCU
